// Logisim project rec.circ as structural Verilog: 1 circuit, main circuit main
module main (
  input  reset,
  input  [7:0] Input1,
  input  [7:0] Input2,
  input  [7:0] Input3,
  output [7:0] out_5
);

  wire clock_out;
  wire [7:0] A_q, adder_1_out, B_q, C_q, multiplier_1_out, Result_reg_2_q, Result_reg_q, subtractor_1_out;

  Clock clock (.out(clock_out));
  Register A (.D(Input1), .Q(A_q), .clk(clock_out), .clr(reset));  // open: en
  Register B (.D(Input2), .Q(B_q), .clk(clock_out), .clr(reset));  // open: en
  Register C (.D(Input3), .Q(C_q), .clk(clock_out), .clr(reset));  // open: en
  Multiplier multiplier_1 (.a(A_q), .b(A_q), .out(multiplier_1_out));  // open: cin, cout
  Register Result_reg (.D(multiplier_1_out), .Q(Result_reg_q), .clr(clock_out));  // open: en, clk
  Register Result_reg_2 (.D(subtractor_1_out), .Q(Result_reg_2_q), .clr(clock_out));  // open: en, clk
  Subtractor subtractor_1 (.a(Result_reg_q), .b(B_q), .out(subtractor_1_out));  // open: bin, bout
  Adder adder_1 (.a(Result_reg_2_q), .b(C_q), .out(adder_1_out));  // open: cin, cout
  Register Result (.D(adder_1_out), .Q(out_5), .clr(clock_out));  // open: en, clk
endmodule
